# Fritzing sketch jhoang6_semesterProjectDiagram (saved by Fritzing 0.9.3b)

parts:
  Part1 = Arduino Uno (Rev3) - ICSP
  Part2 = Adafruit VL53L0X Time of Flight Distance Sensor [part_number="Adafruit #3317"]
  SP1 = SPEAKER [package=pcb_mount_speaker]
  LED1 = LED - 3mm [color="Red (633nm)" package="3 mm [THT]"]
  R1 = Resistor [tolerance=±5% resistance=220 package="2010 [SMD]"]

nets:
  N1: Part1.A4/SDA, Part2.SDA
  N2: Part1.A5/SCL, Part2.SCL
  N3: Part1.D13/SCK, R1.Pin_0
  GND: Part1.GND, Part2.GND, SP1.-, LED1.cathode
  N4: Part1.5V, Part2.2.8V, SP1.+
  N5: LED1.anode, R1.Pin_1

notes:
  time-of-flight laser range sensor
  Speakers
  LED "brake lights"
  Connection to the other arduino with pins 0 and 1

custom parts:
  Adafruit VL53L0X Time of Flight Distance Sensor: The VL53L0X is a Time of Flight distance sensor like no other you've used! The sensor contains a very tiny invisible laser source, and a matching sensor. The VL53L0X can detect the "time of flight", or how long the light has taken to bounce back to the sensor. Since it uses a very narrow light source, it is good for determining distance of only the surface directly in front of it. Unlike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
